// Logisim project eLC-3.circ as structural Verilog: 2 circuits, main circuit eLC-3
module eLC_3 (
);

  wire and_2_out, CLOCK, e0, e1, e2, e3, e4, e5, e6, e7, GateALU, GateMDR, GateOFFSET, GatePC, GateREG,
       LD_CC, LD_IR, LD_MAR, LD_MDR, LD_PC, LD_REG, MEM_EN, MEM_RW, MIO_EN, not_1_out, not_2_out, PCMUX,
       SR2MUX;
  wire [1:0] ALUK;
  wire [2:0] CC_q, comparator_1_gt, IR_2_0, IR_8_6, IR_11_9, SR1;
  wire [3:0] OPCODE;
  wire [4:3] IR_4_0;
  wire [5:5] PCOFF;
  wire [15:0] adder_1_out, adder_2_out, adder_3_out, and_1_out, bit_extender_1_out, bit_extender_2_out,
       controlled_buffer_1_out, MAR_q, MDR_q, multiplexer_1_out, multiplexer_2_out, multiplexer_3_out,
       multiplexer_4_out, multiplexer_5_out, multiplexer_6_out, not_3_out, PC_q, R0, R1, R2, R3, R4, R5, R6,
       R7, ram_1_data;

  assign controlled_buffer_1_out = GateOFFSET ? adder_1_out : 16'bz;  // Controlled_Buffer controlled_buffer_1
  Multiplexer #(.width(16), .enable("false")) multiplexer_1 (
    .in0(adder_1_out), .in1(adder_2_out), .out(multiplexer_1_out), .sel(PCMUX));
  Adder #(.width(16)) adder_1 (.a(bit_extender_1_out), .b(PC_q), .out(adder_1_out), .cin(1'b0));  // open: cout
  assign bit_extender_1_out = {{7{IR_8_6[2]}}, {IR_8_6, PCOFF[5], IR_4_0, IR_2_0}};  // Bit_Extender bit_extender_1
  Register #(.width(16)) IR (
    .D(controlled_buffer_1_out), .en(LD_IR), .Q({OPCODE, IR_11_9, IR_8_6, PCOFF[5], IR_4_0, IR_2_0}),
    .clk(CLOCK));  // open: clr
  Multiplexer #(.width(16), .enable("false")) multiplexer_2 (
    .in0(controlled_buffer_1_out), .in1(ram_1_data), .out(multiplexer_2_out), .sel(MIO_EN));
  assign controlled_buffer_1_out = GatePC ? PC_q : 16'bz;  // Controlled_Buffer controlled_buffer_2
  Register #(.width(16)) PC (.D(multiplexer_1_out), .en(LD_PC), .Q(PC_q), .clk(CLOCK));  // open: clr
  assign controlled_buffer_1_out = GateMDR ? MDR_q : 16'bz;  // Controlled_Buffer controlled_buffer_3
  Register #(.width(16)) MDR (.D(multiplexer_2_out), .en(LD_MDR), .Q(MDR_q), .clk(CLOCK));  // open: clr
  Adder #(.width(16)) adder_2 (.a(PC_q), .b(16'h1), .out(adder_2_out), .cin(1'b0));  // open: cout
  Comparator #(.width(16)) comparator_1 (
    .a(controlled_buffer_1_out), .b({16{1'b0}}), .gt(comparator_1_gt[0]), .eq(comparator_1_gt[1]),
    .lt(comparator_1_gt[2]));
  Clock clock_1 (.out(CLOCK));
  Register #(.width(3)) CC (.D(comparator_1_gt), .en(LD_CC), .Q(CC_q), .clk(CLOCK));  // open: clr
  RAM #(.addrWidth(16), .dataWidth(16), .bus("separate")) ram_1 (
    .addr(MAR_q), .din(MDR_q), .data(ram_1_data), .str(MEM_RW), .sel(MEM_EN), .clk(CLOCK), .ld(not_1_out));  // open: clr
  not not_1 (not_1_out, MEM_RW);
  Demultiplexer #(.select(3), .disabled(0)) demultiplexer_1 (
    .out0(e0), .out1(e1), .out2(e2), .out3(e3), .out4(e4), .out5(e5), .out6(e6), .out7(e7), .in(1'b1),
    .sel(IR_11_9), .en(LD_REG));
  Controller FSM (
    .CLOCK(CLOCK), .IR({OPCODE, IR_11_9, IR_8_6, PCOFF[5], IR_4_0, IR_2_0}), .CC(CC_q), .ALUK(ALUK),
    .GateALU(GateALU), .GateMDR(GateMDR), .GateOFFSET(GateOFFSET), .GatePC(GatePC), .GateREG(GateREG),
    .LD_CC(LD_CC), .LD_IR(LD_IR), .LD_MAR(LD_MAR), .LD_MDR(LD_MDR), .LD_REG(LD_REG), .LD_PC(LD_PC),
    .MEM_EN(MEM_EN), .MEM_RW(MEM_RW), .MIO_EN(MIO_EN), .PCMUX(PCMUX), .SR2MUX(SR2MUX));
  Register #(.width(16)) MAR (.D(controlled_buffer_1_out), .en(LD_MAR), .Q(MAR_q), .clk(CLOCK));  // open: clr
  Register #(.width(16)) u_R0 (.D(controlled_buffer_1_out), .en(e0), .Q(R0), .clk(CLOCK));  // open: clr
  Register #(.width(16)) u_R4 (.D(controlled_buffer_1_out), .en(e4), .Q(R4), .clk(CLOCK));  // open: clr
  Multiplexer #(.select(3), .width(16), .enable("false")) multiplexer_3 (
    .in0(R0), .in1(R1), .in2(R2), .in3(R3), .in4(R4), .in5(R5), .in6(R6), .in7(R7), .out(multiplexer_3_out),
    .sel(IR_2_0));
  assign bit_extender_2_out = {{11{IR_4_0[4]}}, {IR_4_0, IR_2_0}};  // Bit_Extender bit_extender_2
  not not_2 (not_2_out, SR2MUX);
  Multiplexer #(.width(16), .enable("false")) multiplexer_4 (
    .in0(bit_extender_2_out), .in1(multiplexer_3_out), .out(multiplexer_4_out), .sel(not_2_out));
  // Probe on multiplexer_4_out
  Register #(.width(16)) u_R1 (.D(controlled_buffer_1_out), .en(e1), .Q(R1), .clk(CLOCK));  // open: clr
  Register #(.width(16)) u_R5 (.D(controlled_buffer_1_out), .en(e5), .Q(R5), .clk(CLOCK));  // open: clr
  Adder #(.width(16)) adder_3 (
    .a(multiplexer_5_out), .b(multiplexer_4_out), .out(adder_3_out), .cin(1'b0));  // open: cout
  assign and_1_out = multiplexer_5_out & multiplexer_4_out;  // AND_Gate and_1, 16 bits wide
  assign not_3_out = ~multiplexer_5_out;  // NOT_Gate not_3, 16 bits wide
  Register #(.width(16)) u_R2 (.D(controlled_buffer_1_out), .en(e2), .Q(R2), .clk(CLOCK));  // open: clr
  Register #(.width(16)) u_R6 (.D(controlled_buffer_1_out), .en(e6), .Q(R6), .clk(CLOCK));  // open: clr
  Multiplexer #(.select(3), .width(16), .enable("false")) multiplexer_5 (
    .in0(R0), .in1(R1), .in2(R2), .in3(R3), .in4(R4), .in5(R5), .in6(R6), .in7(R7), .out(multiplexer_5_out),
    .sel(SR1));
  // Probe on multiplexer_5_out
  Multiplexer #(.select(2), .width(16), .enable("false")) multiplexer_6 (
    .in0(adder_3_out), .in1(and_1_out), .in2(not_3_out), .out(multiplexer_6_out), .sel(ALUK));  // open: in3
  assign controlled_buffer_1_out = GateALU ? multiplexer_6_out : 16'bz;  // Controlled_Buffer controlled_buffer_4
  Register #(.width(16)) u_R3 (.D(controlled_buffer_1_out), .en(e3), .Q(R3), .clk(CLOCK));  // open: clr
  Register #(.width(16)) u_R7 (.D(controlled_buffer_1_out), .en(e7), .Q(R7), .clk(CLOCK));  // open: clr
  assign controlled_buffer_1_out = GateREG ? multiplexer_5_out : 16'bz;  // Controlled_Buffer GateREG
  and and_2 (and_2_out, OPCODE[0], OPCODE[1], ~OPCODE[2], ~OPCODE[3]);  // AND_Gate
  // Probe on controlled_buffer_1_out
  Multiplexer #(.width(3), .enable("false")) multiplexer_7 (.in0(IR_8_6), .in1(IR_11_9), .out(SR1), .sel(and_2_out));

  // Other names for the same wires on the sheet: IR_4_0[2:0] = IR_2_0; PCOFF (some bits) = {IR_8_6, IR_4_0, IR_2_0}

  // Notes on the sheet:
  //   eLC-3 DATAPATH
  //   INPUT SECTION: Do not change anything here!
  //   To test, load a file into memory and tick the clock.
  //   MEMORY
  //   REG FILE
  //   ALU
  //   LOGIC FOR SR1
endmodule

module Controller (
  input  CLOCK,
  input  [15:0] IR,
  input  [2:0] CC,
  output [1:0] ALUK,
  output GateALU,
  output GateMDR,
  output GateOFFSET,
  output GatePC,
  output GateREG,
  output LD_CC,
  output LD_IR,
  output LD_MAR,
  output LD_MDR,
  output LD_REG,
  output LD_PC,
  output MEM_EN,
  output MEM_RW,
  output MIO_EN,
  output PCMUX,
  output SR2MUX
);

  wire _1, _2, _5, _6, _7, _8, _9, _10, _11, _12, _13, _14, _16, and_1_out, and_2_out, and_3_out, or_1_out,
       S0, S0n_out, S1, S1n_out, S2, S2n_out, undriven, undriven_2, undriven_3, undriven_4, undriven_5,
       undriven_6, undriven_7, undriven_8, undriven_9;

  and and_1 (and_1_out, CC[2], IR[11]);
  and and_2 (and_2_out, CC[1], IR[10]);
  or or_1 (or_1_out, and_1_out, and_2_out, and_3_out);
  and and_3 (and_3_out, CC[0], IR[9]);
  and Fetch_1 (_1, ~S2, ~S1, ~S0);  // AND_Gate
  and Fetch_2 (_2, ~S2, ~S1, S0);  // AND_Gate
  and Fetch_3 (LD_IR, ~S2, S1, ~S0);  // AND_Gate
  and NOT_4 (ALUK[1], IR[15], ~IR[14], ~IR[13], IR[12], ~S2, S1, S0);  // AND_Gate
  and ADDS_4 (_5, ~IR[15], ~IR[14], ~IR[13], IR[12], ~S2, S1, S0, ~IR[5]);  // AND_Gate
  and ADDI_4 (_6, ~IR[15], ~IR[14], ~IR[13], IR[12], ~S2, S1, S0, IR[5]);  // AND_Gate
  and ANDS_4 (_7, ~IR[15], IR[14], ~IR[13], IR[12], ~S2, S1, S0, ~IR[5]);  // AND_Gate
  and ANDI_4 (_8, ~IR[15], IR[14], ~IR[13], IR[12], ~S2, S1, S0, IR[5]);  // AND_Gate
  and LD_4 (_9, ~IR[15], ~IR[14], IR[13], ~IR[12], ~S2, S1, S0);  // AND_Gate
  and LD_5 (_10, IR[15], ~IR[14], IR[13], ~IR[12], S2, ~S1, ~S0);  // AND_Gate
  and LD_6 (_11, ~IR[15], IR[14], IR[13], ~IR[12], S2, ~S1, S0);  // AND_Gate
  and BRHit_4 (_12, ~IR[15], ~IR[14], ~IR[13], ~IR[12], ~S2, S1, S0, or_1_out);  // AND_Gate
  and BR_nHit (_13, ~IR[15], ~IR[14], ~IR[13], ~IR[12], ~S2, S1, S0, ~or_1_out);  // AND_Gate
  and ST_4 (_14, ~IR[15], ~IR[14], IR[13], IR[12], ~S2, S1, S0);  // AND_Gate
  and ST_5 (GateREG, IR[15], ~IR[14], IR[13], IR[12], S2, ~S1, ~S0);  // AND_Gate
  and ST_6 (_16, ~IR[15], IR[14], IR[13], IR[12], S2, ~S1, S0);  // AND_Gate
  or S2n (S2n_out, _9, _10, _14, GateREG);
  or or_2 (MIO_EN, _2, _10);
  or or_3 (GateMDR, LD_IR, _11);
  or or_4 (PCMUX, _1, _13);
  // OR_Gate or_5 has open pins: in0=undriven, in1=undriven, in2=undriven_2, in3=undriven_3, in4=undriven_3, out=open
  or or_6 (LD_CC, ALUK[1], _5, _6, _7, _8, _11);
  D_Flip_Flop u_S2 (.clk(CLOCK), .D(S2n_out), .Q(S2));  // open: Qn, preset, en, reset
  D_Flip_Flop u_S1 (.clk(CLOCK), .D(S1n_out), .Q(S1));  // open: Qn, preset, en, reset
  D_Flip_Flop u_S0 (.clk(CLOCK), .D(S0n_out), .Q(S0));  // open: Qn, preset, en, reset
  or S1n (S1n_out, _2, LD_IR);
  buf or_7 (MEM_RW, _16);  // OR_Gate
  or or_8 (LD_MAR, _1, _9, _13, _14);
  or or_9 (LD_PC, _1, _12, _13);
  or or_10 (ALUK[0], _7, _8);
  or or_11 (LD_REG, ALUK[1], _5, _6, _7, _8, _11);
  or S0n (S0n_out, _1, LD_IR, _10, _13, GateREG);
  or or_12 (MEM_EN, _2, _10, _16);
  or or_13 (LD_MDR, _2, _10, GateREG);
  or or_14 (GatePC, _1, _13);
  or or_15 (SR2MUX, _6, _8);
  // OR_Gate or_16 has open pins: in0=undriven_4, in1=undriven_4, in2=undriven_5, in3=undriven_6, in4=undriven_6, out=open
  or or_17 (GateOFFSET, _9, _14);
  or or_18 (GateALU, ALUK[1], _5, _6, _7, _8);
  // OR_Gate or_19 has open pins: in0=undriven_7, in1=undriven_7, in2=undriven_8, in3=undriven_9, in4=undriven_9, out=open

  // Other names for the same wires on the sheet: _3 = LD_IR; _15 = GateREG; ALUKL = ALUK[0]; _4 = ALUK[1];
  //   ALUKM = ALUK[1]; GateOFF = GateOFFSET

  // Notes on the sheet:
  //   eLC-3 CONTROLLER
  //   INPUT SECTION: Do not change anything here!
  //   You may only change the values of the inputs for testing using the hand tool.
  //   Do not introduce a clock or any other input or output pins in the circuit.
  //   NZP
  //   To your logic
  //   OUTPUT SECTION: Do not change anything here!
  //   Do not introduce a clock any other input or output pins in the circuit.
  //   From your logic
endmodule
